# Fritzing sketch PhaseTwo_ROUTED (saved by Fritzing 0.9.3b)
breadboards: 8

parts:
  Raspberry_Pi_Model_4_B = Raspberry Pi 4B
  PD1_1_5MOhm = Resistor [tolerance=±0.1% resistance=1.5M package=THT]
  PD19_1_5MOhm = Resistor [tolerance=±0.1% resistance=1.5M package=THT]
  PD20_1_5MOhm = Resistor [tolerance=±0.1% resistance=1.5M package=THT]
  PD21_1_5MOhm = Resistor [tolerance=±0.1% resistance=1.5M package=THT]
  PD2_1_5MOhm = Resistor [tolerance=±0.1% resistance=1.5M package=THT]
  PD22_1_5MOhm = Resistor [tolerance=±0.1% resistance=1.5M package=THT]
  PD16_1_5MOhm = Resistor [tolerance=±0.1% resistance=1.5M package=THT]
  PD24_1_5MOhm = Resistor [tolerance=±0.1% resistance=1.5M package=THT]
  PD23_1_5MOhm = Resistor [tolerance=±0.1% resistance=1.5M package=THT]
  PD17_1_5MOhm = Resistor [tolerance=±0.1% resistance=1.5M package=THT]
  PD5_1_5MOhm = Resistor [tolerance=±0.1% resistance=1.5M package=THT]
  PD15_1_5MOhm = Resistor [tolerance=±0.1% resistance=1.5M package=THT]
  PD4_1_5MOhm = Resistor [tolerance=±0.1% resistance=1.5M package=THT]
  PD18_1_5MOhm = Resistor [tolerance=±0.1% resistance=1.5M package=THT]
  PD8_1_5MOhm = Resistor [tolerance=±0.1% resistance=1.5M package=THT]
  PD6_1_5MOhm = Resistor [tolerance=±0.1% resistance=1.5M package=THT]
  PD10_1_5MOhm = Resistor [tolerance=±0.1% resistance=1.5M package=THT]
  PD9_1_5MOhm = Resistor [tolerance=±0.1% resistance=1.5M package=THT]
  PD12_1_5MOhm = Resistor [tolerance=±0.1% resistance=1.5M package=THT]
  PD14_1_5MOhm = Resistor [tolerance=±0.1% resistance=1.5M package=THT]
  PD7_1_5MOhm = Resistor [tolerance=±0.1% resistance=1.5M package=THT]
  PD11_1_5MOhm = Resistor [tolerance=±0.1% resistance=1.5M package=THT]
  HC-SR04_First_Three_Lasers = hc-sr04
  HC_SR04_1_1k_INPUT_GND = Resistor [tolerance=±5% resistance=1k package=THT]
  HC_SR04_1_1k_GND = Resistor [tolerance=±5% resistance=1k package=THT]
  HC_SR04_1_1k_ECHO = Resistor [tolerance=±5% resistance=1k package=THT]
  HC_SR04_Second_Three_Lasers = hc-sr04
  HC_SR04_2_1k_GND = Resistor [tolerance=±5% resistance=1k package=THT]
  HC_SR04_2_1k_INPUT_GND = Resistor [tolerance=±5% resistance=1k package=THT]
  HC_SR04_2_1k_ECHO = Resistor [tolerance=±5% resistance=1k package=THT]
  HC_SR04_Lasers_7&8 = hc-sr04
  HC_SR04_3_1k_GND = Resistor [tolerance=±5% resistance=1k package=THT]
  HC_SR04_3_1k_INPUT_GND = Resistor [tolerance=±5% resistance=1k package=THT]
  HC_SR04_3_1k_ECHO = Resistor [tolerance=±5% resistance=1k package=THT]
  Foot_Pedal_(Pushbutton) = Pushbutton [package="[SMD]"]
  First_12_Photodiodes_MCP23017 = MCP23017 [package="DIP (Dual Inline) [THT]"]
  Second_12_Photodiode_MCP23017 = MCP23017 [package="DIP (Dual Inline) [THT]"]
  Laser1_68_Ohm = Resistor [tolerance=±1% resistance=68 package=THT]
  Laser2_68_Ohm = Resistor [tolerance=±1% resistance=68 package=THT]
  Laser3_68_Ohm = Resistor [tolerance=±1% resistance=68 package=THT]
  Laser4_68_Ohm = Resistor [tolerance=±1% resistance=68 package=THT]
  Laser5_68_Ohm = Resistor [tolerance=±1% resistance=68 package=THT]
  Laser6_68_Ohm = Resistor [tolerance=±1% resistance=68 package=THT]
  Laser7_68_Ohm = Resistor [tolerance=±1% resistance=68 package=THT]
  Laser12_68_Ohm = Resistor [tolerance=±1% resistance=68 package=THT]
  Laser11_68_Ohm = Resistor [tolerance=±1% resistance=68 package=THT]
  Laser8_68_Ohm = Resistor [tolerance=±1% resistance=68 package=THT]
  Laser10_68_Ohm = Resistor [tolerance=±1% resistance=68 package=THT]
  Laser9_68_Ohm = Resistor [tolerance=±1% resistance=68 package=THT]
  Laser17_68_Ohm = Resistor [tolerance=±1% resistance=68 package=THT]
  Laser22_68_Ohm = Resistor [tolerance=±1% resistance=68 package=THT]
  Laser21_68_Ohm = Resistor [tolerance=±1% resistance=68 package=THT]
  Laser18_68_Ohm = Resistor [tolerance=±1% resistance=68 package=THT]
  Laser20_68_Ohm = Resistor [tolerance=±1% resistance=68 package=THT]
  Laser19_68_Ohm = Resistor [tolerance=±1% resistance=68 package=THT]
  Laser23_68_Ohm = Resistor [tolerance=±1% resistance=68 package=THT]
  Laser16_68_Ohm = Resistor [tolerance=±1% resistance=68 package=THT]
  Laser15_68_Ohm = Resistor [tolerance=±1% resistance=68 package=THT]
  Laser24_68_Ohm = Resistor [tolerance=±1% resistance=68 package=THT]
  Laser14_68_Ohm = Resistor [tolerance=±1% resistance=68 package=THT]
  Laser13_68_Ohm = Resistor [tolerance=±1% resistance=68 package=THT]
  Laser1_130_Ohm = Resistor [tolerance=±1% resistance=130 package=THT]
  Laser2_130_Ohm = Resistor [tolerance=±1% resistance=130 package=THT]
  Laser3_130_Ohm = Resistor [tolerance=±1% resistance=130 package=THT]
  Laser4_130_Ohm = Resistor [tolerance=±1% resistance=130 package=THT]
  Laser5_130_Ohm = Resistor [tolerance=±1% resistance=130 package=THT]
  Laser6_130_Ohm = Resistor [tolerance=±1% resistance=130 package=THT]
  Laser8_130_Ohm = Resistor [tolerance=±1% resistance=130 package=THT]
  Laser7_130_Ohm = Resistor [tolerance=±1% resistance=130 package=THT]
  Laser9_130_Ohm = Resistor [tolerance=±1% resistance=130 package=THT]
  Laser11_130_Ohm = Resistor [tolerance=±1% resistance=130 package=THT]
  Laser10_130_Ohm = Resistor [tolerance=±1% resistance=130 package=THT]
  Laser12_130_Ohm = Resistor [tolerance=±1% resistance=130 package=THT]
  Laser18_130_Ohm = Resistor [tolerance=±1% resistance=130 package=THT]
  Laser17_130_Ohm = Resistor [tolerance=±1% resistance=130 package=THT]
  Laser19_130_Ohm = Resistor [tolerance=±1% resistance=130 package=THT]
  Laser21_130_Ohm = Resistor [tolerance=±1% resistance=130 package=THT]
  Laser20_130_Ohm = Resistor [tolerance=±1% resistance=130 package=THT]
  Laser22_130_Ohm = Resistor [tolerance=±1% resistance=130 package=THT]
  Laser15_130_Ohm = Resistor [tolerance=±1% resistance=130 package=THT]
  Laser23_130_Ohm = Resistor [tolerance=±1% resistance=130 package=THT]
  Laser16_130_Ohm = Resistor [tolerance=±1% resistance=130 package=THT]
  Laser14_130_Ohm = Resistor [tolerance=±1% resistance=130 package=THT]
  Laser13_130_Ohm = Resistor [tolerance=±1% resistance=130 package=THT]
  Laser24_130_Ohm = Resistor [tolerance=±1% resistance=130 package=THT]
  Laser1 = LED - 3mm [color="Red (660nm)" package="3 mm [THT]"]
  Laser2 = LED - 3mm [color="Red (660nm)" package="3 mm [THT]"]
  Laser3 = LED - 3mm [color="Red (660nm)" package="3 mm [THT]"]
  Laser4 = LED - 3mm [color="Red (660nm)" package="3 mm [THT]"]
  Laser5 = LED - 3mm [color="Red (660nm)" package="3 mm [THT]"]
  Laser6 = LED - 3mm [color="Red (660nm)" package="3 mm [THT]"]
  Laser7 = LED - 3mm [color="Red (660nm)" package="3 mm [THT]"]
  Laser8 = LED - 3mm [color="Red (660nm)" package="3 mm [THT]"]
  Laser9 = LED - 3mm [color="Red (660nm)" package="3 mm [THT]"]
  Laser10 = LED - 3mm [color="Red (660nm)" package="3 mm [THT]"]
  Laser11 = LED - 3mm [color="Red (660nm)" package="3 mm [THT]"]
  Laser12 = LED - 3mm [color="Red (660nm)" package="3 mm [THT]"]
  Laser13 = LED - 3mm [color="Red (660nm)" package="3 mm [THT]"]
  Laser14 = LED - 3mm [color="Red (660nm)" package="3 mm [THT]"]
  Laser15 = LED - 3mm [color="Red (660nm)" package="3 mm [THT]"]
  Laser16 = LED - 3mm [color="Red (660nm)" package="3 mm [THT]"]
  Laser17 = LED - 3mm [color="Red (660nm)" package="3 mm [THT]"]
  Laser18 = LED - 3mm [color="Red (660nm)" package="3 mm [THT]"]
  Laser19 = LED - 3mm [color="Red (660nm)" package="3 mm [THT]"]
  Laser20 = LED - 3mm [color="Red (660nm)" package="3 mm [THT]"]
  Laser21 = LED - 3mm [color="Red (660nm)" package="3 mm [THT]"]
  Laser22 = LED - 3mm [color="Red (660nm)" package="3 mm [THT]"]
  Laser23 = LED - 3mm [color="Red (660nm)" package="3 mm [THT]"]
  Laser24 = LED - 3mm [color="Red (660nm)" package="3 mm [THT]"]
  Photodiode_1 = SFH213 Si Photodiode [package="8mm Ceramic [THT]"]
  Photodiode_2 = SFH213 Si Photodiode [package="8mm Ceramic [THT]"]
  Photodiode_3 = SFH213 Si Photodiode [package="8mm Ceramic [THT]"]
  Photodiode_4 = SFH213 Si Photodiode [package="8mm Ceramic [THT]"]
  Photodiode_5 = SFH213 Si Photodiode [package="8mm Ceramic [THT]"]
  Photodiode_6 = SFH213 Si Photodiode [package="8mm Ceramic [THT]"]
  Photodiode_7 = SFH213 Si Photodiode [package="8mm Ceramic [THT]"]
  Photodiode_8 = SFH213 Si Photodiode [package="8mm Ceramic [THT]"]
  Photodiode_9 = SFH213 Si Photodiode [package="8mm Ceramic [THT]"]
  Photodiode_10 = SFH213 Si Photodiode [package="8mm Ceramic [THT]"]
  Photodiode_11 = SFH213 Si Photodiode [package="8mm Ceramic [THT]"]
  Photodiode_12 = SFH213 Si Photodiode [package="8mm Ceramic [THT]"]
  Photodiode_14 = SFH213 Si Photodiode [package="8mm Ceramic [THT]"]
  Photodiode_15 = SFH213 Si Photodiode [package="8mm Ceramic [THT]"]
  Photodiode_16 = SFH213 Si Photodiode [package="8mm Ceramic [THT]"]
  Photodiode_17 = SFH213 Si Photodiode [package="8mm Ceramic [THT]"]
  Photodiode_18 = SFH213 Si Photodiode [package="8mm Ceramic [THT]"]
  Photodiode_19 = SFH213 Si Photodiode [package="8mm Ceramic [THT]"]
  Photodiode_20 = SFH213 Si Photodiode [package="8mm Ceramic [THT]"]
  Photodiode_22 = SFH213 Si Photodiode [package="8mm Ceramic [THT]"]
  Photodiode_23 = SFH213 Si Photodiode [package="8mm Ceramic [THT]"]
  Photodiode_24 = SFH213 Si Photodiode [package="8mm Ceramic [THT]"]
  Laser_Switch = Toggle Switch [package=THT]
  PD3_1_5MOhm = Resistor [tolerance=±0.1% resistance=1.5M package=THT]
  PD13_1_5MOhm = Resistor [tolerance=±0.1% resistance=1.5M package=THT]
  Foot_Pedal_Current_Limiting_Sensor = Resistor [tolerance=±5% resistance=330 package=THT]
  Photodiode_13 = SFH213 Si Photodiode [package="8mm Ceramic [THT]"]
  Photodiode_21 = SFH213 Si Photodiode [package="8mm Ceramic [THT]"]

nets (from the schematic view):
  VCC: Raspberry_Pi_Model_4_B.3V3, Foot_Pedal_(Pushbutton).Pin_3, Foot_Pedal_(Pushbutton).Pin_4, First_12_Photodiodes_MCP23017.VCC, First_12_Photodiodes_MCP23017.RST, Second_12_Photodiode_MCP23017.VCC, Second_12_Photodiode_MCP23017.A0, Second_12_Photodiode_MCP23017.RST
  VCC_2: Raspberry_Pi_Model_4_B.5V, HC-SR04_First_Three_Lasers.VCC, HC_SR04_Second_Three_Lasers.VCC, HC_SR04_Lasers_7&8.VCC, Laser_Switch.L1
  N1: Raspberry_Pi_Model_4_B.GPIO2, First_12_Photodiodes_MCP23017.SDA, Second_12_Photodiode_MCP23017.SDA
  N2: Raspberry_Pi_Model_4_B.GPIO3, First_12_Photodiodes_MCP23017.SCL, Second_12_Photodiode_MCP23017.SCL
  GND: Raspberry_Pi_Model_4_B.GND, HC-SR04_First_Three_Lasers.GND, HC_SR04_1_1k_GND.Pin_1, HC_SR04_Second_Three_Lasers.GND, HC_SR04_2_1k_GND.Pin_1, HC_SR04_3_1k_GND.Pin_1, First_12_Photodiodes_MCP23017.GND, First_12_Photodiodes_MCP23017.A0, First_12_Photodiodes_MCP23017.A1, First_12_Photodiodes_MCP23017.A2, Second_12_Photodiode_MCP23017.GND, Second_12_Photodiode_MCP23017.A1, Second_12_Photodiode_MCP23017.A2, Laser1_68_Ohm.Pin_1, Laser2_68_Ohm.Pin_1, Laser3_68_Ohm.Pin_1, Laser4_68_Ohm.Pin_1, Laser5_68_Ohm.Pin_1, Laser6_68_Ohm.Pin_1, Laser7_68_Ohm.Pin_1, Laser12_68_Ohm.Pin_1, Laser11_68_Ohm.Pin_1, Laser8_68_Ohm.Pin_1, Laser10_68_Ohm.Pin_1, Laser9_68_Ohm.Pin_1, Laser17_68_Ohm.Pin_1, Laser22_68_Ohm.Pin_1, Laser21_68_Ohm.Pin_1, Laser18_68_Ohm.Pin_1, Laser20_68_Ohm.Pin_1, Laser19_68_Ohm.Pin_1, Laser23_68_Ohm.Pin_1, Laser16_68_Ohm.Pin_1, Laser15_68_Ohm.Pin_1, Laser24_68_Ohm.Pin_1, Laser14_68_Ohm.Pin_1, Laser13_68_Ohm.Pin_1, Photodiode_1.anode, Photodiode_2.anode, Photodiode_3.anode, Photodiode_4.anode, Photodiode_5.anode, Photodiode_6.anode, Photodiode_7.anode, Photodiode_8.anode, Photodiode_9.anode, Photodiode_10.anode, Photodiode_11.anode, Photodiode_12.anode, Photodiode_14.anode, Photodiode_15.anode, Photodiode_16.anode, Photodiode_17.anode, Photodiode_18.anode, Photodiode_19.anode, Photodiode_20.anode, Photodiode_22.anode, Photodiode_23.anode, Photodiode_24.anode, Laser_Switch.L2, Foot_Pedal_Current_Limiting_Sensor.Pin_0, Photodiode_13.anode, Photodiode_21.anode
  N3: Raspberry_Pi_Model_4_B.GPIO14, HC-SR04_First_Three_Lasers.Trig
  N4: Raspberry_Pi_Model_4_B.GPIO15, HC_SR04_1_1k_INPUT_GND.Pin_1, HC_SR04_1_1k_ECHO.Pin_0
  N5: Raspberry_Pi_Model_4_B.GPIO18, HC_SR04_Second_Three_Lasers.Trig
  N6: Raspberry_Pi_Model_4_B.GPIO23, HC_SR04_2_1k_INPUT_GND.Pin_1, HC_SR04_2_1k_ECHO.Pin_0
  N7: Raspberry_Pi_Model_4_B.GPIO25, HC_SR04_Lasers_7&8.Trig
  N8: Raspberry_Pi_Model_4_B.GPIO8, HC_SR04_3_1k_INPUT_GND.Pin_1, HC_SR04_3_1k_ECHO.Pin_0
  N9: PD1_1_5MOhm.Pin_0, PD19_1_5MOhm.Pin_0, PD20_1_5MOhm.Pin_0, PD21_1_5MOhm.Pin_0, PD2_1_5MOhm.Pin_0, PD22_1_5MOhm.Pin_0, PD16_1_5MOhm.Pin_0, PD24_1_5MOhm.Pin_0, PD23_1_5MOhm.Pin_0, PD17_1_5MOhm.Pin_0, PD5_1_5MOhm.Pin_0, PD15_1_5MOhm.Pin_0, PD4_1_5MOhm.Pin_0, PD18_1_5MOhm.Pin_0, PD8_1_5MOhm.Pin_0, PD6_1_5MOhm.Pin_0, PD10_1_5MOhm.Pin_0, PD9_1_5MOhm.Pin_0, PD12_1_5MOhm.Pin_0, PD14_1_5MOhm.Pin_0, PD7_1_5MOhm.Pin_0, PD11_1_5MOhm.Pin_0, PD3_1_5MOhm.Pin_0, PD13_1_5MOhm.Pin_0
  N10: PD1_1_5MOhm.Pin_1, First_12_Photodiodes_MCP23017.GPA4, Photodiode_1.cathode
  N11: PD19_1_5MOhm.Pin_1, Second_12_Photodiode_MCP23017.GPB2, Photodiode_19.cathode
  N12: PD20_1_5MOhm.Pin_1, Second_12_Photodiode_MCP23017.GPB3, Photodiode_20.cathode
  N13: PD21_1_5MOhm.Pin_1, Second_12_Photodiode_MCP23017.GPB4, Photodiode_21.cathode
  N14: PD2_1_5MOhm.Pin_1, First_12_Photodiodes_MCP23017.GPA5, Photodiode_2.cathode
  N15: PD22_1_5MOhm.Pin_1, Second_12_Photodiode_MCP23017.GPB5, Photodiode_22.cathode
  N16: PD16_1_5MOhm.Pin_1, Second_12_Photodiode_MCP23017.GPA7, Photodiode_16.cathode
  N17: PD24_1_5MOhm.Pin_1, Second_12_Photodiode_MCP23017.GPB7, Photodiode_24.cathode
  N18: PD23_1_5MOhm.Pin_1, Second_12_Photodiode_MCP23017.GPB6, Photodiode_23.cathode
  N19: PD17_1_5MOhm.Pin_1, Second_12_Photodiode_MCP23017.GPB0, Photodiode_17.cathode
  N20: PD5_1_5MOhm.Pin_1, First_12_Photodiodes_MCP23017.GPB0, Photodiode_5.cathode
  N21: PD15_1_5MOhm.Pin_1, Second_12_Photodiode_MCP23017.GPA6, Photodiode_15.cathode
  N22: PD4_1_5MOhm.Pin_1, First_12_Photodiodes_MCP23017.GPA7, Photodiode_4.cathode
  N23: PD18_1_5MOhm.Pin_1, Second_12_Photodiode_MCP23017.GPB1, Photodiode_18.cathode
  N24: PD8_1_5MOhm.Pin_1, First_12_Photodiodes_MCP23017.GPB3, Photodiode_8.cathode
  N25: PD6_1_5MOhm.Pin_1, First_12_Photodiodes_MCP23017.GPB1, Photodiode_6.cathode
  N26: PD10_1_5MOhm.Pin_1, First_12_Photodiodes_MCP23017.GPB5, Photodiode_10.cathode
  N27: PD9_1_5MOhm.Pin_1, First_12_Photodiodes_MCP23017.GPB4, Photodiode_9.cathode
  N28: PD12_1_5MOhm.Pin_1, First_12_Photodiodes_MCP23017.GPB7, Photodiode_12.cathode
  N29: PD14_1_5MOhm.Pin_1, Second_12_Photodiode_MCP23017.GPA5, Photodiode_14.cathode
  N30: PD7_1_5MOhm.Pin_1, First_12_Photodiodes_MCP23017.GPB2, Photodiode_7.cathode
  N31: PD11_1_5MOhm.Pin_1, First_12_Photodiodes_MCP23017.GPB6, Photodiode_11.cathode
  N32: HC-SR04_First_Three_Lasers.Echo, HC_SR04_1_1k_ECHO.Pin_1
  N33: HC_SR04_1_1k_INPUT_GND.Pin_0, HC_SR04_1_1k_GND.Pin_0
  N34: HC_SR04_Second_Three_Lasers.Echo, HC_SR04_2_1k_ECHO.Pin_1
  N35: HC_SR04_2_1k_GND.Pin_0, HC_SR04_2_1k_INPUT_GND.Pin_0
  N36: HC_SR04_Lasers_7&8.Echo, HC_SR04_3_1k_ECHO.Pin_1
  N37: HC_SR04_3_1k_GND.Pin_0, HC_SR04_3_1k_INPUT_GND.Pin_0
  N38: Foot_Pedal_(Pushbutton).Pin_1, Foot_Pedal_(Pushbutton).Pin_2, First_12_Photodiodes_MCP23017.GPA0, Foot_Pedal_Current_Limiting_Sensor.Pin_1
  N39: First_12_Photodiodes_MCP23017.GPA6, Photodiode_3.cathode, PD3_1_5MOhm.Pin_1
  N40: Second_12_Photodiode_MCP23017.GPA4, PD13_1_5MOhm.Pin_1, Photodiode_13.cathode
  N41: Laser1_68_Ohm.Pin_0, Laser1.cathode
  N42: Laser2_68_Ohm.Pin_0, Laser2.cathode
  N43: Laser3_68_Ohm.Pin_0, Laser3.cathode
  N44: Laser4_68_Ohm.Pin_0, Laser4.cathode
  N45: Laser5_68_Ohm.Pin_0, Laser5.cathode
  N46: Laser6_68_Ohm.Pin_0, Laser6.cathode
  N47: Laser7_68_Ohm.Pin_0, Laser7.cathode
  N48: Laser12_68_Ohm.Pin_0, Laser12.cathode
  N49: Laser11_68_Ohm.Pin_0, Laser11.cathode
  N50: Laser8_68_Ohm.Pin_0, Laser8.cathode
  N51: Laser10_68_Ohm.Pin_0, Laser10.cathode
  N52: Laser9_68_Ohm.Pin_0, Laser9.cathode
  N53: Laser17_68_Ohm.Pin_0, Laser17.cathode
  N54: Laser22_68_Ohm.Pin_0, Laser22.cathode
  N55: Laser21_68_Ohm.Pin_0, Laser21.cathode
  N56: Laser18_68_Ohm.Pin_0, Laser18.cathode
  N57: Laser20_68_Ohm.Pin_0, Laser20.cathode
  N58: Laser19_68_Ohm.Pin_0, Laser19.cathode
  N59: Laser23_68_Ohm.Pin_0, Laser23.cathode
  N60: Laser16_68_Ohm.Pin_0, Laser16.cathode
  N61: Laser15_68_Ohm.Pin_0, Laser15.cathode
  N62: Laser24_68_Ohm.Pin_0, Laser24.cathode
  N63: Laser14_68_Ohm.Pin_0, Laser14.cathode
  N64: Laser13_68_Ohm.Pin_0, Laser13.cathode
  N65: Laser1_130_Ohm.Pin_0, Laser2_130_Ohm.Pin_0, Laser3_130_Ohm.Pin_0, Laser4_130_Ohm.Pin_0, Laser5_130_Ohm.Pin_0, Laser6_130_Ohm.Pin_0, Laser8_130_Ohm.Pin_0, Laser7_130_Ohm.Pin_0, Laser9_130_Ohm.Pin_0, Laser11_130_Ohm.Pin_0, Laser10_130_Ohm.Pin_0, Laser12_130_Ohm.Pin_0, Laser18_130_Ohm.Pin_0, Laser17_130_Ohm.Pin_0, Laser19_130_Ohm.Pin_0, Laser21_130_Ohm.Pin_0, Laser20_130_Ohm.Pin_0, Laser22_130_Ohm.Pin_0, Laser15_130_Ohm.Pin_0, Laser23_130_Ohm.Pin_0, Laser16_130_Ohm.Pin_0, Laser14_130_Ohm.Pin_0, Laser13_130_Ohm.Pin_0, Laser24_130_Ohm.Pin_0, Laser_Switch.COM
  N66: Laser1_130_Ohm.Pin_1, Laser1.anode
  N67: Laser2_130_Ohm.Pin_1, Laser2.anode
  N68: Laser3_130_Ohm.Pin_1, Laser3.anode
  N69: Laser4_130_Ohm.Pin_1, Laser4.anode
  N70: Laser5_130_Ohm.Pin_1, Laser5.anode
  N71: Laser6_130_Ohm.Pin_1, Laser6.anode
  N72: Laser8_130_Ohm.Pin_1, Laser8.anode
  N73: Laser7_130_Ohm.Pin_1, Laser7.anode
  N74: Laser9_130_Ohm.Pin_1, Laser9.anode
  N75: Laser11_130_Ohm.Pin_1, Laser11.anode
  N76: Laser10_130_Ohm.Pin_1, Laser10.anode
  N77: Laser12_130_Ohm.Pin_1, Laser12.anode
  N78: Laser18_130_Ohm.Pin_1, Laser18.anode
  N79: Laser17_130_Ohm.Pin_1, Laser17.anode
  N80: Laser19_130_Ohm.Pin_1, Laser19.anode
  N81: Laser21_130_Ohm.Pin_1, Laser21.anode
  N82: Laser20_130_Ohm.Pin_1, Laser20.anode
  N83: Laser22_130_Ohm.Pin_1, Laser22.anode
  N84: Laser15_130_Ohm.Pin_1, Laser15.anode
  N85: Laser23_130_Ohm.Pin_1, Laser23.anode
  N86: Laser16_130_Ohm.Pin_1, Laser16.anode
  N87: Laser14_130_Ohm.Pin_1, Laser14.anode
  N88: Laser13_130_Ohm.Pin_1, Laser13.anode
  N89: Laser24_130_Ohm.Pin_1, Laser24.anode

notes:
  Ignore this power rail
  Circuits to represent the laser system. The red wire represents the laser diode itself and the upper resistor is the attached 130 Ohm resistor. This is alongside 68 Ohm resistor

custom parts:
  MCP23017: 16 bit I/O chip controlled via I2C
  SFH213 Si Photodiode: S1133 photodiode with low dark current by Hamamatsu.
